// Logisim project 自动.circ as structural Verilog: 18 circuits, main circuit 显示
module _8_3 (
  input  in_1,
  input  in_2,
  input  in_3,
  input  in_4,
  input  in_5,
  input  in_6,
  input  in_7,
  input  in_8,
  output out_9,
  output out_10,
  output out_11
);

  wire not_2_out, not_3_out, not_4_out, not_5_out, not_6_out, not_7_out, not_8_out;

  // NOT_Gate not_1 has open pins: in=in_1, out=open
  not not_2 (not_2_out, in_2);
  not not_3 (not_3_out, in_3);
  not not_4 (not_4_out, in_4);
  not not_5 (not_5_out, in_5);
  not not_6 (not_6_out, in_6);
  not not_7 (not_7_out, in_7);
  not not_8 (not_8_out, in_8);
  nand nand_1 (out_9, not_2_out, not_4_out, not_6_out, not_8_out);
  nand nand_2 (out_10, not_3_out, not_4_out, not_7_out, not_8_out);
  nand nand_3 (out_11, not_5_out, not_6_out, not_7_out, not_8_out);
endmodule

module _3_8 (
  input  in_1,
  input  in_2,
  input  in_3,
  output out_4,
  output out_5,
  output out_6,
  output out_7,
  output out_8,
  output out_9,
  output out_10,
  output out_11
);

  wire not_1_out, not_2_out, not_3_out;

  not not_1 (not_1_out, in_1);
  not not_2 (not_2_out, in_2);
  not not_3 (not_3_out, in_3);
  and and_1 (out_4, not_1_out, not_2_out, not_3_out);
  and and_2 (out_5, in_1, not_3_out, not_2_out);
  and and_3 (out_6, not_1_out, in_2, not_3_out);
  and and_4 (out_7, in_2, in_1, not_3_out);
  and and_5 (out_8, not_1_out, in_3, not_2_out);
  and and_6 (out_9, not_2_out, in_3, in_1);
  and and_7 (out_10, not_1_out, in_2, in_3);
  and and_8 (out_11, in_2, in_3, in_1);
endmodule

module \显示  (
  input  in_1,
  input  in_2,
  input  in_3,
  input  in_4,
  input  in_5,
  input  in_6,
  input  in_7,
  input  in_8,
  input  in_9,
  input  in_10,
  input  in_11,
  input  in_12,
  input  in_13,
  input  in_14,
  input  in_15,
  input  in_16,
  input  in_17
);

  wire n3_8_1_out_4, n3_8_1_out_5, n3_8_1_out_6, n3_8_1_out_7, n3_8_1_out_8, n3_8_1_out_9, n3_8_1_out_10,
       n3_8_1_out_11, n8_3_1_out_9, n8_3_1_out_10, n8_3_1_out_11, n8_3_2_out_9, n8_3_2_out_10, n8_3_2_out_11,
       \加法_1_out_7 , \加法_1_out_8 , \加法_1_out_9 , \加法_1_out_10 , \寄存_1_out_5 , \寄存_1_out_6 , \寄存_1_out_7 ,
       \寄存_2_out_5 , \寄存_2_out_6 , \寄存_2_out_7 , \寄存_3_out_5 , \寄存_3_out_6 , \寄存_3_out_7 , \控制_1_out_5 ,
       \控制_1_out_6 , \控制_1_out_7 , \灯_1_out_5 , \灯_1_out_6 , \灯_1_out_7 , \灯_1_out_8 , \灯_1_out_9 ,
       \灯_1_out_10 , \灯_1_out_11 , \自动控制_1_out_9 , \自动控制_1_out_10 , \自动控制_1_out_11 , \自动控制_1_out_12 ,
       \自动控制_1_out_13 , \自动控制_1_out_14 , \计数_1_out_2 , \计数_1_out_3 , \计数_1_out_4 ;

  _8_3 u_8_3_1 (
    .in_1(in_2), .in_2(in_3), .in_3(in_4), .in_4(in_5), .in_5(in_6), .in_6(in_7), .in_7(in_8), .in_8(in_9),
    .out_9(n8_3_1_out_9), .out_10(n8_3_1_out_10), .out_11(n8_3_1_out_11));
  _8_3 u_8_3_2 (
    .in_1(in_10), .in_2(in_11), .in_3(in_12), .in_4(in_13), .in_5(in_14), .in_6(in_15), .in_7(in_16),
    .in_8(in_17), .out_9(n8_3_2_out_9), .out_10(n8_3_2_out_10), .out_11(n8_3_2_out_11));
  \控制  \u_控制_1  (
    .in_1(\自动控制_1_out_9 ), .in_2(n8_3_1_out_9), .in_3(n8_3_1_out_10), .in_4(n8_3_1_out_11),
    .out_5(\控制_1_out_5 ), .out_6(\控制_1_out_6 ), .out_7(\控制_1_out_7 ));
  \控制  \u_控制_2  (
    .in_1(\自动控制_1_out_11 ), .in_2(n8_3_2_out_9), .in_3(n8_3_2_out_10), .in_4(n8_3_2_out_11),
    .out_5(\控制_1_out_5 ), .out_6(\控制_1_out_6 ), .out_7(\控制_1_out_7 ));
  LED led_1 (.in(\控制_1_out_6 ));
  LED led_2 (.in(\控制_1_out_7 ));
  LED led_3 (.in(\控制_1_out_5 ));
  \灯  \u_灯_1  (
    .in_1(1'b0), .in_2(\控制_1_out_7 ), .in_3(\控制_1_out_6 ), .in_4(\控制_1_out_5 ), .out_5(\灯_1_out_5 ),
    .out_6(\灯_1_out_6 ), .out_7(\灯_1_out_7 ), .out_8(\灯_1_out_8 ), .out_9(\灯_1_out_9 ),
    .out_10(\灯_1_out_10 ), .out_11(\灯_1_out_11 ));
  \寄存  \u_寄存_1  (
    .in_1(\控制_1_out_7 ), .in_2(\控制_1_out_6 ), .in_3(\控制_1_out_5 ), .in_4(\自动控制_1_out_10 ),
    .out_5(\寄存_1_out_5 ), .out_6(\寄存_1_out_6 ), .out_7(\寄存_1_out_7 ));
  \寄存  \u_寄存_2  (
    .in_1(\控制_1_out_7 ), .in_2(\控制_1_out_6 ), .in_3(\控制_1_out_5 ), .in_4(\自动控制_1_out_12 ),
    .out_5(\寄存_2_out_5 ), .out_6(\寄存_2_out_6 ), .out_7(\寄存_2_out_7 ));
  _7_Segment_Display u_7_segment_display_1 (
    .g(\灯_1_out_11 ), .f(\灯_1_out_10 ), .a(\灯_1_out_5 ), .b(\灯_1_out_6 ), .e(\灯_1_out_9 ), .d(\灯_1_out_8 ),
    .c(\灯_1_out_7 ), .dp(1'b0));
  LED led_4 (.in(\加法_1_out_7 ));
  \加法  \u_加法_1  (
    .in_1(\寄存_1_out_5 ), .in_2(\寄存_1_out_6 ), .in_3(\寄存_1_out_7 ), .in_4(\寄存_2_out_5 ), .in_5(\寄存_2_out_6 ),
    .in_6(\寄存_2_out_7 ), .out_7(\加法_1_out_7 ), .out_8(\加法_1_out_8 ), .out_9(\加法_1_out_9 ),
    .out_10(\加法_1_out_10 ));
  \寄存  \u_寄存_3  (
    .in_1(\加法_1_out_8 ), .in_2(\加法_1_out_9 ), .in_3(\加法_1_out_10 ), .in_4(\自动控制_1_out_13 ),
    .out_5(\寄存_3_out_5 ), .out_6(\寄存_3_out_6 ), .out_7(\寄存_3_out_7 ));
  \计数  \u_计数_1  (.in_1(in_1), .out_2(\计数_1_out_2 ), .out_3(\计数_1_out_3 ), .out_4(\计数_1_out_4 ));
  \控制  \u_控制_3  (
    .in_1(\自动控制_1_out_14 ), .in_2(\寄存_3_out_5 ), .in_3(\寄存_3_out_6 ), .in_4(\寄存_3_out_7 ),
    .out_5(\控制_1_out_7 ), .out_6(\控制_1_out_6 ), .out_7(\控制_1_out_5 ));
  _3_8 u_3_8_1 (
    .in_1(\计数_1_out_2 ), .in_2(\计数_1_out_3 ), .in_3(\计数_1_out_4 ), .out_4(n3_8_1_out_4),
    .out_5(n3_8_1_out_5), .out_6(n3_8_1_out_6), .out_7(n3_8_1_out_7), .out_8(n3_8_1_out_8),
    .out_9(n3_8_1_out_9), .out_10(n3_8_1_out_10), .out_11(n3_8_1_out_11));
  \自动控制  \u_自动控制_1  (
    .in_1(n3_8_1_out_11), .in_2(n3_8_1_out_10), .in_3(n3_8_1_out_9), .in_4(n3_8_1_out_8),
    .in_5(n3_8_1_out_7), .in_6(n3_8_1_out_6), .in_7(n3_8_1_out_5), .in_8(n3_8_1_out_4),
    .out_9(\自动控制_1_out_9 ), .out_10(\自动控制_1_out_10 ), .out_11(\自动控制_1_out_11 ), .out_12(\自动控制_1_out_12 ),
    .out_13(\自动控制_1_out_13 ), .out_14(\自动控制_1_out_14 ));
  LED led_5 (.in(n3_8_1_out_4));
  LED led_6 (.in(n3_8_1_out_5));
  LED led_7 (.in(n3_8_1_out_6));
  LED led_8 (.in(n3_8_1_out_7));
  LED led_9 (.in(n3_8_1_out_8));
  LED led_10 (.in(n3_8_1_out_9));
  LED led_11 (.in(n3_8_1_out_10));
  LED led_12 (.in(n3_8_1_out_11));
endmodule

module a (
  input  in_1,
  input  in_2,
  input  in_3,
  input  in_4,
  output out_5
);

  wire and_1_out, and_2_out, not_1_out, not_2_out;

  not not_1 (not_1_out, in_4);
  and and_1 (and_1_out, in_2, in_4);
  not not_2 (not_2_out, in_2);
  and and_2 (and_2_out, not_2_out, not_1_out);
  or or_1 (out_5, and_1_out, in_1, and_2_out, in_3);
endmodule

module b (
  input  in_1,
  input  in_2,
  input  in_3,
  input  in_4,
  output out_5
);

  wire and_1_out, and_2_out, not_1_out, not_2_out, not_3_out;

  not not_1 (not_1_out, in_2);
  and and_1 (and_1_out, in_3, in_4);
  not not_2 (not_2_out, in_4);
  not not_3 (not_3_out, in_3);
  and and_2 (and_2_out, not_2_out, not_3_out);
  or or_1 (out_5, not_1_out, and_1_out, and_2_out);
endmodule

module c (
  input  in_1,
  input  in_2,
  input  in_3,
  input  in_4,
  output out_5
);

  wire not_1_out;

  not not_1 (not_1_out, in_3);
  or or_1 (out_5, in_2, in_4, not_1_out);
endmodule

module d (
  input  in_1,
  input  in_2,
  input  in_3,
  input  in_4,
  output out_5
);

  wire and_1_out, and_2_out, and_3_out, and_4_out, not_1_out, not_2_out, not_3_out;

  not not_1 (not_1_out, in_2);
  not not_2 (not_2_out, in_3);
  not not_3 (not_3_out, in_4);
  and and_1 (and_1_out, in_3, not_3_out);
  and and_2 (and_2_out, not_1_out, in_3);
  and and_3 (and_3_out, not_1_out, not_3_out);
  and and_4 (and_4_out, in_4, in_2, not_2_out);
  or or_1 (out_5, in_1, and_1_out, and_2_out, and_3_out, and_4_out);
endmodule

module e (
  input  in_1,
  input  in_2,
  input  in_3,
  input  in_4,
  output out_5
);

  wire and_1_out, and_2_out, not_1_out, not_2_out;

  not not_1 (not_1_out, in_4);
  and and_1 (and_1_out, not_1_out, in_3);
  not not_2 (not_2_out, in_2);
  and and_2 (and_2_out, not_2_out, not_1_out);
  or or_1 (out_5, and_1_out, and_2_out);
endmodule

module f (
  input  in_1,
  input  in_2,
  input  in_3,
  input  in_4,
  output out_5
);

  wire and_1_out, and_2_out, and_3_out, not_1_out, not_2_out, not_3_out;

  not not_1 (not_1_out, in_2);
  not not_2 (not_2_out, in_3);
  not not_3 (not_3_out, in_4);
  and and_1 (and_1_out, not_1_out, not_2_out, not_3_out);
  and and_2 (and_2_out, in_2, not_2_out);
  and and_3 (and_3_out, in_2, in_3, not_3_out);
  or or_1 (out_5, in_1, and_1_out, and_2_out, and_3_out);
endmodule

module g (
  input  in_1,
  input  in_2,
  input  in_3,
  input  in_4,
  output out_5
);

  wire and_1_out, and_2_out, and_3_out, not_1_out, not_2_out, not_3_out, not_4_out;

  not not_1 (not_1_out, in_1);
  not not_2 (not_2_out, in_2);
  not not_3 (not_3_out, in_3);
  not not_4 (not_4_out, in_4);
  and and_1 (and_1_out, in_2, not_3_out);
  and and_2 (and_2_out, in_3, not_1_out, not_2_out);
  and and_3 (and_3_out, in_3, not_4_out);
  or or_1 (out_5, in_1, and_1_out, and_2_out, and_3_out);
endmodule

module \灯  (
  input  in_1,
  input  in_2,
  input  in_3,
  input  in_4,
  output out_5,
  output out_6,
  output out_7,
  output out_8,
  output out_9,
  output out_10,
  output out_11
);

  a a_1 (.in_1(in_1), .in_2(in_2), .in_3(in_3), .in_4(in_4), .out_5(out_5));
  b b_1 (.in_1(in_1), .in_2(in_2), .in_3(in_3), .in_4(in_4), .out_5(out_6));
  c c_1 (.in_1(in_1), .in_2(in_2), .in_3(in_3), .in_4(in_4), .out_5(out_7));
  d d_1 (.in_1(in_1), .in_2(in_2), .in_3(in_3), .in_4(in_4), .out_5(out_8));
  e e_1 (.in_1(in_1), .in_2(in_2), .in_3(in_3), .in_4(in_4), .out_5(out_9));
  f f_1 (.in_2(in_1), .in_1(in_2), .in_3(in_3), .in_4(in_4), .out_5(out_10));
  g g_1 (.in_1(in_1), .in_2(in_2), .in_3(in_3), .in_4(in_4), .out_5(out_11));
endmodule

module \控制  (
  input  in_1,
  input  in_2,
  input  in_3,
  input  in_4,
  output out_5,
  output out_6,
  output out_7
);

  assign out_5 = in_1 ? in_2 : 1'bz;  // Controlled_Buffer controlled_buffer_1
  assign out_6 = in_1 ? in_3 : 1'bz;  // Controlled_Buffer controlled_buffer_2
  assign out_7 = in_1 ? in_4 : 1'bz;  // Controlled_Buffer controlled_buffer_3
endmodule

module \寄存  (
  input  in_1,
  input  in_2,
  input  in_3,
  input  in_4,
  output out_5,
  output out_6,
  output out_7
);

  D_Flip_Flop d_ff_1 (.clk(in_4), .D(in_1), .Q(out_5));  // open: Qn, preset, en, reset
  D_Flip_Flop d_ff_2 (.clk(in_4), .D(in_2), .Q(out_6));  // open: Qn, preset, en, reset
  D_Flip_Flop d_ff_3 (.clk(in_4), .D(in_3), .Q(out_7));  // open: Qn, preset, en, reset
endmodule

module \半加  (
  input  in_1,
  input  in_2,
  output out_3,
  output out_4
);

  and and_1 (out_4, in_1, in_1, in_2);
  xor xor_1 (out_3, in_2, in_1);
endmodule

module \全加  (
  input  in_1,
  input  in_2,
  input  in_3,
  output out_4,
  output out_5
);

  wire \半加_1_out_3 , \半加_1_out_4 , \半加_2_out_4 ;

  \半加  \u_半加_1  (.in_1(in_2), .in_2(in_3), .out_3(\半加_1_out_3 ), .out_4(\半加_1_out_4 ));
  \半加  \u_半加_2  (.in_1(in_1), .in_2(\半加_1_out_3 ), .out_3(out_4), .out_4(\半加_2_out_4 ));
  or or_1 (out_5, \半加_2_out_4 , \半加_1_out_4 );
endmodule

module \加法  (
  input  in_1,
  input  in_2,
  input  in_3,
  input  in_4,
  input  in_5,
  input  in_6,
  output out_7,
  output out_8,
  output out_9,
  output out_10
);

  wire \全加_1_out_5 , \全加_2_out_5 ;

  \全加  \u_全加_1  (.in_1(1'b0), .in_2(in_3), .in_3(in_6), .out_4(out_10), .out_5(\全加_1_out_5 ));
  \全加  \u_全加_2  (.in_1(\全加_1_out_5 ), .in_2(in_2), .in_3(in_5), .out_4(out_9), .out_5(\全加_2_out_5 ));
  \全加  \u_全加_3  (.in_1(\全加_2_out_5 ), .in_2(in_1), .in_3(in_4), .out_4(out_8), .out_5(out_7));
endmodule

module \计数  (
  input  in_1,
  output out_2,
  output out_3,
  output out_4
);

  wire clock_1_out, not_1_out, not_2_out;

  Clock clock_1 (.out(clock_1_out));
  not not_1 (not_1_out, out_3);
  T_Flip_Flop t_ff_1 (.clk(clock_1_out), .T(in_1), .Q(out_2));  // open: Qn, preset, reset, en
  not not_2 (not_2_out, out_2);
  T_Flip_Flop t_ff_2 (.clk(not_2_out), .T(in_1), .Q(out_3));  // open: Qn, preset, reset, en
  T_Flip_Flop t_ff_3 (.clk(not_1_out), .T(in_1), .Q(out_4));  // open: Qn, preset, reset, en
endmodule

module \自动控制  (
  input  in_1,
  input  in_2,
  input  in_3,
  input  in_4,
  input  in_5,
  input  in_6,
  input  in_7,
  input  in_8,
  output out_9,
  output out_10,
  output out_11,
  output out_12,
  output out_13,
  output out_14
);

  wire n8_3_1_out_9, n8_3_1_out_10, n8_3_1_out_11, not_1_out, not_2_out;

  _8_3 u_8_3_1 (
    .in_1(in_1), .in_2(in_2), .in_3(in_3), .in_4(in_4), .in_5(in_5), .in_6(in_6), .in_7(in_7), .in_8(in_8),
    .out_9(n8_3_1_out_9), .out_10(n8_3_1_out_10), .out_11(n8_3_1_out_11));
  not not_1 (not_1_out, n8_3_1_out_9);
  not not_2 (not_2_out, n8_3_1_out_10);
  // NOT_Gate not_3 has open pins: in=n8_3_1_out_11, out=open
  and and_1 (out_9, not_1_out, not_2_out);
  and and_2 (out_10, not_1_out, not_2_out, n8_3_1_out_11);
  and and_3 (out_11, not_1_out, n8_3_1_out_10);
  and and_4 (out_12, not_1_out, n8_3_1_out_10, n8_3_1_out_11);
  and and_5 (out_13, not_2_out, not_1_out, n8_3_1_out_9);
  buf and_6 (out_14, n8_3_1_out_9);  // AND_Gate
endmodule
